# Fritzing sketch Pinout (saved by Fritzing 0.9.4)
breadboards: 1

parts:
  HC-SR04_Sensor_1 = HC-SR04 Ultrasonic Distance Sensor
  HC-SR04_Sensor_2 = HC-SR04 Ultrasonic Distance Sensor
  HC-SR04_Sensor_3 = HC-SR04 Ultrasonic Distance Sensor
  J2 = STM32 Nucleo boards
  DC_Mot_Enc1 = DC Motor with two-phase hall-encoder [part_number=VT-E-G25A-06-177E]
  DC_Mot_Enc2 = DC Motor with two-phase hall-encoder [part_number=VT-E-G25A-06-177E]
  DC_Mot_Enc3 = DC Motor with two-phase hall-encoder [part_number=VT-E-G25A-06-177E]
  DC_Mot_Enc4 = DC Motor with two-phase hall-encoder [part_number=VT-E-G25A-06-177E]
  GY1 = MPU-6050 Board GY-521 [form="♀ (female)" package=THT]
  M1 = ps2 gamepad [package=THT]
  IC2 = IC, DIP package, 8 pins [chip_label=IC]  # not connected
  J1 = STM32 Nucleo boards
  Sabertooth_2x1 = Sabertooth 2x12
  Sabertooth_2x2 = Sabertooth 2x12
  U1 = LM2596 step down module
  BATT1 = LiPoly Battery (1300mAh)
  U2 = LUXEON-REBEL [package=luxeon-rebel]
  U3 = LUXEON-REBEL [package=luxeon-rebel]
  KY-1 = Keyes Relay [package=THT]
  U4 = DIODE-ZENER [package=diode-zener]
  U5 = DIODE-ZENER [package=diode-zener]
  J3 = Piezo Speaker
  KY-2 = Keyes Relay [package=THT]

nets:
  VCC: HC-SR04_Sensor_1.VCC, HC-SR04_Sensor_2.VCC, HC-SR04_Sensor_3.VCC, J2.E5V, DC_Mot_Enc1.pin1, DC_Mot_Enc2.pin1, DC_Mot_Enc3.pin1, DC_Mot_Enc4.pin1, GY1.pin1, M1.3.3V, U1.OUT+, KY-1.power, KY-2.power, KY-2.C
  N1: HC-SR04_Sensor_1.TRIG, J2.A5/SCL#115
  N2: HC-SR04_Sensor_1.ECHO, J2.A0
  GND: HC-SR04_Sensor_1.GND, HC-SR04_Sensor_2.GND, HC-SR04_Sensor_3.GND, J2.GND, DC_Mot_Enc1.pin2, DC_Mot_Enc2.pin2, DC_Mot_Enc3.pin2, DC_Mot_Enc4.pin2, GY1.pin2, M1.GND, J1.GND, Sabertooth_2x1.0v, Sabertooth_2x1.B-, Sabertooth_2x2.0v, Sabertooth_2x2.B-, U1.IN-, U1.OUT-, BATT1.negative, U2.S, U3.S, KY-1.ground, KY-1.C, J3.pin1, KY-2.ground
  N3: HC-SR04_Sensor_2.TRIG, J2.A3
  N4: HC-SR04_Sensor_2.ECHO, J2.D9_PWM
  N5: HC-SR04_Sensor_3.TRIG, J2.A4/SDA#114
  N6: HC-SR04_Sensor_3.ECHO, J2.A1
  N7: J2.A2, J1.A5/SCL#1160
  N8: J2.PC6, J1.D2
  N9: J2.PA12, J1.D10_PWM/SS
  N10: J2.D10_PWM/SS, Sabertooth_2x1.S1
  N11: J2.D11_PWM/MOSI, M1.CMD
  N12: J2.D12/MISO, M1.DAT
  N13: J2.D13/SCK, M1.CLK
  N14: J2.A4/SDA#1159, J1.A4/SDA#1159
  N15: J2.A5/SCL#1160, U4.A
  N16: J2.D2, J1.D4
  N17: J2.D4, J1.D5_PWM
  N18: J2.D5_PWM, GY1.pin4
  N19: J2.D6_PWM, M1.ATT
  N20: J2.D7, GY1.pin3
  N21: J2.PC3, KY-2.signal
  N22: DC_Mot_Enc1.pin3, Sabertooth_2x2.M2B
  N23: DC_Mot_Enc1.pin4, J1.D3_PWM
  N24: DC_Mot_Enc1.pin5, J1.D13/SCK
  N25: DC_Mot_Enc1.pin6, Sabertooth_2x2.M2A
  N26: DC_Mot_Enc2.pin3, Sabertooth_2x1.M2B
  N27: DC_Mot_Enc2.pin4, J1.A1
  N28: DC_Mot_Enc2.pin5, J1.A0
  N29: DC_Mot_Enc2.pin6, Sabertooth_2x1.M2A
  N30: DC_Mot_Enc3.pin3, Sabertooth_2x2.M1A
  N31: DC_Mot_Enc3.pin4, J1.D8
  N32: DC_Mot_Enc3.pin5, J1.D7
  N33: DC_Mot_Enc3.pin6, Sabertooth_2x2.M1B
  N34: DC_Mot_Enc4.pin3, Sabertooth_2x1.M1A
  N35: DC_Mot_Enc4.pin4, J1.D11_PWM/MOSI
  N36: DC_Mot_Enc4.pin5, J1.D12/MISO
  N37: DC_Mot_Enc4.pin6, Sabertooth_2x1.M1B
  N38: J1.A3, J3.pin2
  N39: J1.A4/SDA#114, U2.C
  N40: J1.A5/SCL#115, U3.C
  N41: J1.E5V, KY-2.NC
  N42: J1.D6_PWM, U5.A
  N43: Sabertooth_2x1.B+, Sabertooth_2x2.B+, U1.IN+, BATT1.positive, U2.A, U3.A
  N44: Sabertooth_2x2.S2, KY-1.NO
  N45: KY-1.signal, U4.C

custom parts:
  MPU-6050 Board GY-521: Acelerometro y Giroscopio MPU-6050 Board GY-521
  ps2 gamepad: PS2 gamepad. Warning! PCB view is designed for the female connector available from https://www.robotshop.com/en/ps2-connector.html. However there is no mechanical information that I can find so ipcb was generated from a scaled jpg and may well be wrong. Print the footprint out and check it against a real part before ordering boards!
  LM2596 step down module: LM2596 DC-DC step down power supply module 3 A.
  LiPoly Battery (1300mAh): Lithium Ion Polymer Battery (1300mAh)
  Keyes Relay: The Keyes 5V relay module is suitable for SCM development, home appliance control. It uses a 5V~12V TIL control signal which can control DC / AC signal.
